# Fritzing sketch schematic (saved by Fritzing 1.0.0rc)
breadboards: 1

parts:
  I2C_SSD1315_128x64 = OLED 128x64 I2C Monochrome Display
  Mod1 = Amica NodeMCU DEVKIT 1.0
  E3Z-R61 = E18-D80NK_1 [mn=or mpn=E3Z-LAS-R8 part_number="(NPN NO)" package=THT]
  S1 = Pushbutton [package="[THT]"]
  R1 = Resistor [tolerance=±5% resistance=10k package="0402 [SMD]"]
  A1 = MH-FMD buzzer

nets:
  N1: I2C_SSD1315_128x64.SDA, Mod1.pin_13
  N2: I2C_SSD1315_128x64.SCK, Mod1.pin_14
  N3: I2C_SSD1315_128x64.VDD, Mod1.pin1, Mod1.pin_10, Mod1.pin_26, R1.Pin_1
  N4: I2C_SSD1315_128x64.GND, Mod1.pin2, Mod1.pin_9, Mod1.pin_25, Mod1.pin_29, E3Z-R61.pin1, S1.Pin_1, S1.Pin_2, A1.Pin_3
  N5: Mod1.pin4, E3Z-R61.pin3
  N6: Mod1.pin6, A1.Pin_2
  N7: Mod1.pin8, S1.Pin_3, S1.Pin_4, R1.Pin_0
  N8: Mod1.pin_30, E3Z-R61.pin2, A1.Pin_1

notes:
  +3V
  GND
  +5V
  You can power the entire board either through the MicroUSB port on the NodeMCU module or via the VCC and GND pins.

custom parts:
  E18-D80NK_1: E18-D80NK Proximity Sensor module.
  MH-FMD buzzer: MH-FMD buzzer.
