# Fritzing sketch schematic4 (saved by Fritzing 1.0.0rc)
breadboards: 1

parts:
  I2C_SSD1315_128x64 = OLED 128x64 I2C Monochrome Display
  E3Z-R61 = E18-D80NK_1 [mn=or part_number="(NPN NO)" mpn=E3Z-LAS-R8 package=THT]
  S1 = Pushbutton [package="[THT]"]
  WeMos_D1_Mini1 = WeMos D1 Mini  # not connected
  1N4728A_3_3V = DIODE-ZENER [package=diode-zener]
  R2 = Resistor [tolerance=±5% resistance=10k package="2512 [SMD]"]
  R1 = Resistor [tolerance=±5% resistance=10k package="0402 [SMD]"]
  DC_Boost_Board_5v_to_12v = mini boost module
  A1 = MH-FMD buzzer

nets:
  N1: I2C_SSD1315_128x64.GND, E3Z-R61.pin1, S1.Pin_1, S1.Pin_2, 1N4728A_3_3V.C, DC_Boost_Board_5v_to_12v.Pin_1, A1.Pin_3
  N2: E3Z-R61.pin2, R2.Pin_1, DC_Boost_Board_5v_to_12v.Pin_4
  N3: E3Z-R61.pin3, R2.Pin_0
  N4: S1.Pin_3, S1.Pin_4, R1.Pin_0
  N5: DC_Boost_Board_5v_to_12v.Pin_2, A1.Pin_1

notes:
  +3V
  GND
  +5V
  You can power the entire board either through the MicroUSB port on the Wemos module or via the 5V and G (GND) pins. The laser sensor is powered by a DC-Booster board that converts 5V to 12V.

custom parts:
  E18-D80NK_1: E18-D80NK Proximity Sensor module.
  mini boost module: mini boost module.
  MH-FMD buzzer: MH-FMD buzzer.
